# Fritzing sketch Balcony_Watering system (saved by Fritzing 0.9.3b)
circuit board: 8.46667cm x 5.64444cm
breadboards: 1

parts:
  Arduino_WiFi_1010_MKR = Arduino MKR WIFI 1010
  5V_Relay = KY-019 5V Relay Module [package="Breakout board"]
  WATER_PUMP1 = water pump/motor  # not connected
  12V_SLA_Battery_6_5AH = 12 battery [package=battery]
  12-24V_Solar_Panel = Solar Panel [package="Renogy 50 Watts 12 Volt Monocrystalline Bendable Solar Panel"]
  SOLAR_MANAGEMENT_POWER_BOARD = Solar Charge Controller [part_number="HGX Series Solar Charge Controller PWM" package=PWM-Model]
  Float_Switch = Round Pushbutton
  LED1 = LED - 5mm [color="Red (633nm)" package="5 mm [THT]"]
  R1 = Resistor [tolerance=±5% resistance=220 package=THT]
  DHT22_Humidity_and_Temperature_sensor = Humidity and Temperature Sensor RHT03
  Raspberry_Pi_2 = Raspberry Pi 4 [part_number=RPI-4-b]
  LED2 = LED - 5mm [color="Red (633nm)" package="5 mm [THT]"]
  R2 = Resistor [tolerance=±5% resistance=220 package=THT]

nets:
  N1: Arduino_WiFi_1010_MKR.A2, Arduino_WiFi_1010_MKR.GND, 5V_Relay.-, R1.Pin_0, DHT22_Humidity_and_Temperature_sensor.GND_2
  N2: Arduino_WiFi_1010_MKR.D2_PWM, DHT22_Humidity_and_Temperature_sensor.Data-signal
  N3: Arduino_WiFi_1010_MKR.D3_PWM, 5V_Relay.+
  N4: 5V_Relay.S, Float_Switch.leg1, DHT22_Humidity_and_Temperature_sensor.Vcc
  N5: 5V_Relay.Common, SOLAR_MANAGEMENT_POWER_BOARD.Connector_5
  N6: 12V_SLA_Battery_6_5AH.-, SOLAR_MANAGEMENT_POWER_BOARD.Connector_4
  N7: 12V_SLA_Battery_6_5AH.+, 12-24V_Solar_Panel.Connector_1, SOLAR_MANAGEMENT_POWER_BOARD.Connector_2, SOLAR_MANAGEMENT_POWER_BOARD.Connector_3
  N8: 12-24V_Solar_Panel.Connector_2, SOLAR_MANAGEMENT_POWER_BOARD.Connector_1
  N9: Float_Switch.leg0, LED1.anode
  N10: LED1.cathode, R1.Pin_1
  N11: Raspberry_Pi_2.GPIO21, LED2.anode
  N12: Raspberry_Pi_2.GND, R2.Pin_1

custom parts:
  Arduino MKR WIFI 1010: The MKR WIFI 1010 is a significant improvement on the MKR 1000 WIFI. It's equipped with an ESP32 module made by U-BLOX. This board aims to speed up and simplify the prototyping of WiFi based IoT applications thanks to the flexibility of the ESP32 module and its low power consumption. The board is composed of three main blocks: SAMD21 Cortex-M0+ 32bit Low Power ARM MCU; U-BLOX NINA-W10 Series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
  KY-019 5V Relay Module: KY-019 5V Relay module, used to control AC circuits. (Special thanks to vanepp for fixing the PCB holes and other errors)
  water pump/motor: WATER PUMP BY ARDUBLOCKTR
  12 battery: 12V lead acid type battery, like the Husqvarna YTH2448 12V 35AH battery. This is the mini version 1/4 the size of the actual battery to be closer to typical breadboard parts (around 2in wide rathher than 7in). The pads in pcb are sized to accomidate up to 14ga wire (as these batterys will deliver high currents.)
  Solar Panel: Renogy 50 Watts 12 Volt Solar Panel
  Solar Charge Controller: PWM-Solar Charge Controller
  Raspberry Pi 4: The RPi4, a faster version of the awesome Raspberry Pi 2 B ARM Board with 40 pin gpio. Ready for special Raspberry Pi B+ and RPi2 Hat (Hardware attached (on) top)
